# Fritzing sketch KimestuNoSauna (saved by Fritzing 0.9.8b)
breadboards: 1

parts:
  MCU1 = Raspberry Pi Zero
  パーツ1 = LCD1602-I2C
  S1 = Pushbutton [package="[THT]"]
  BAT1 = BC9VPC [package=bc9vpc]
  KY-1 = Keyes Relay [package=THT]
  パーツ3 = Adafruit SHT31-D Sensirion Temperature/Humidity Sensor [part_number="Adafruit #2857"]
  WATER_PUMP1 = water pump/motor
  S2 = Pushbutton [package="[THT]"]
  パーツ4 = NeoPixel Stick [part_number=8128]

nets:
  N1: MCU1.pin_1, MCU1.pin_17, KY-1.ground, パーツ3.VIN
  VCC: MCU1.pin_2, MCU1.pin_4, パーツ1.VCC, パーツ4.+5V
  N2: MCU1.pin_3, パーツ1.SDA, パーツ3.SDA
  N3: MCU1.pin_5, MCU1.pin_7, パーツ1.SCL, パーツ3.SCL
  GND: MCU1.pin_6, MCU1.pin_9, MCU1.pin_10, MCU1.pin_11, MCU1.pin_12, MCU1.pin_14, MCU1.pin_16, MCU1.pin_18, MCU1.pin_19, MCU1.pin_20, MCU1.pin_25, MCU1.pin_34, MCU1.pin_39, パーツ1.GND, S1.Pin_1, S1.Pin_2, S1.Pin_3, S1.Pin_4, KY-1.power, パーツ3.GND, S2.Pin_2, S2.Pin_3, S2.Pin_4, パーツ4.GND
  N4: MCU1.pin_22, MCU1.pin_23, MCU1.pin_24, KY-1.signal
  N5: MCU1.pin_40, パーツ4.DATAIN
  N6: BAT1.V+, KY-1.NO
  N7: BAT1.V-, WATER_PUMP1.pin_1
  N8: KY-1.C, WATER_PUMP1.pin_2

notes:
  鬼滅刀タクトスイッチ
  鬼滅刀連動
  3m延長ケーブルでハンダ付け加工
  (各種指示用スイッチ
  押下でGPIO25制御)
  GND
  GPIO24
  SHT-31
  I2C
  3mの延長ケーブル
  I2C(3.3V,GND,SDA,SCL)
  リレー
  3.3V
  GND
  GPIO25
  RaspberryPi ZeroWH
  LCD1602
  I2C(5V,GND,SDA,SCL)
  Shutdown用タクトスイッチ
  GND
  GPIO18
  ポンプ
  UPSLON 小型水中ポンプ 直流DC5V-DC12V 池ポンプ 揚程3m 給水/排水ポンプ
  鬼滅刀LED
  鬼滅刀連動
  3m延長ケーブルでハンダ付け加工
  5.0V
  GND
  GPIO21

custom parts:
  LCD1602-I2C: A standard character display, usually with 2x16 characters. Comes in many colors with LCM1602 IIC attached.
  Keyes Relay: The Keyes 5V relay module is suitable for SCM development, home appliance control. It uses a 5V~12V TIL control signal which can control DC / AC signal.
  Adafruit SHT31-D Sensirion Temperature/Humidity Sensor: Sensirion Temperature/Humidity sensors are some of the finest & highest-accuracy devices you can get. And, finally we have some that have a true I2C interface for easy reading. The SHT31-D sensor has an excellent ±2% relative humidity and ±0.3°C accuracy for most uses. Unlike earlier SHT sensors, this sensor has a true I2C interface, and (bonus!) even with two address options. It also is 3V or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
  water pump/motor: WATER PUMP BY ARDUBLOCKTR
  NeoPixel Stick: Make your own little LED strip arrangement with this stick of NeoPixel LEDs. We crammed 8 of the tiny 5050 (5mm x 5mm) smart RGB LEDs onto a PCB with mounting holes and a chainable design. Use only one microcontroller pin to control as many as you can chain together! Each LED is addressable as the driver chip is inside the LED. Each one has ~18mA constant current drive so the color will be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
